# Fritzing sketch desain rancangan final (saved by Fritzing 0.9.3b)
breadboards: 1

parts:
  Part1 = Arduino Nano (Rev3.0) (ICSP)
  J1 = Basic Servo
  U1 = ESP8266 WiFi Module [part_number=ESP8266]
  R1 = Resistor [tolerance=±5% resistance=220 package="0805 [SMD]"]
  R2 = Resistor [tolerance=±5% resistance=220 package="0805 [SMD]"]

nets:
  GND: Part1.GND, J1.gnd, U1.GND, R2.Pin_1
  N1: Part1.D2, U1.TXD
  N2: Part1.D3, R1.Pin_0, R2.Pin_0
  N3: Part1.D9, J1.pulse
  VCC: Part1.5V, J1.vcc, U1.VCC, U1.CH_PD
  N4: U1.RXD, R1.Pin_1

custom parts:
  ESP8266 WiFi Module: Generic WiFi Module based on the ESP8266 with onboard PCB antenna and UART communications
