# Fritzing sketch desain rancangan (saved by Fritzing 0.9.3b)
breadboards: 1

parts:
  Part1 = Arduino Nano (Rev3.0) (ICSP)
  U1 = ESP8266 WiFi Module [part_number=ESP8266]
  J1 = Basic Servo
  VCC1 = Battery block 9V

nets:
  N1: Part1.D1/TX, U1.TXD
  N2: Part1.D0/RX, U1.RXD
  GND: Part1.GND, U1.GND, J1.gnd, VCC1.-
  N3: Part1.D2, J1.pulse
  N4: Part1.VIN, VCC1.+
  5V: Part1.5V, J1.vcc
  3V3: Part1.3V3, U1.VCC, U1.CH_PD

custom parts:
  ESP8266 WiFi Module: Generic WiFi Module based on the ESP8266 with onboard PCB antenna and UART communications
